# Fritzing sketch schematic (saved by Fritzing 0.9.4)
circuit board: 8.47cm x 5.64444cm
breadboards: 1

parts:
  U1 = NodeMCU V3.0
  RTC1 = DS3231 AT24C32 Real Time Clock
  C1 = Electrolytic Capacitor [package="100 mil [THT, electrolytic]"]
  Mod1 = KY-018 Photoresistor Module [package="Breakout board"]
  U2 = WS2812 RGB LED strip
  U3 = WS2812 RGB LED strip
  J1 = Power Jack [package=power_jack_pth]
  IC1 = IC, DIP package, 20 pins [chip_label=SN74HCT245N]
  R2 = Resistor [tolerance=±5% resistance=470 package=THT]
  R3 = Resistor [tolerance=±5% resistance=470 package=THT]

nets:
  N1: U1.D1, RTC1.SCL
  N2: U1.D2, RTC1.SDA
  GND: U1.GND#6, U1.GND#13, U1.GND#16, U1.GND#33, RTC1.GND, C1.-, Mod1.-, U2.GND, U3.GND, J1.GND, IC1.pin10, IC1.pin19
  N3: U1.D5, IC1.pin2
  N4: U1.D6, IC1.pin3
  VCC: U1.Vin, RTC1.VCC, C1.+, Mod1.Vin, U2.VCC, U3.VCC, J1.PWR, IC1.pin1, IC1.pin20
  N5: U1.A0, Mod1.S
  N6: U2.DIN, R2.Pin_0
  N7: U3.DIN, R3.Pin_0
  N8: IC1.pin17, R3.Pin_1
  N9: IC1.pin18, R2.Pin_1

custom parts:
  NodeMCU V3.0: ESP8266 based NodeMCU
  DS3231 AT24C32 Real Time Clock: Real-time clock basedo on chip DS3231, plus memory chip AT24C32 (32 Kb storage capacity). On-chip temperature sensor with an accuracy of ±3 ℃, I2C bus interface maximum speed: 400 kHz. Operating voltage: 3.3 V to 5.5 V with battery backup capabilities.
  Electrolytic Capacitor: A small electrolytic capacitor
  KY-018 Photoresistor Module: KY-018 Photoresistor module, used to measure light intensity. It can determine the presence or absence of light.
  WS2812 RGB LED strip: WS2812 strip
